# Fritzing sketch M27C4001-35xFI_to_MB7124E (saved by Fritzing 0.9.6b)
circuit board: 2.08422cm x 5.53935cm
breadboards: 1

parts:
  J1 = female pin header, 16 pins [form="♀ (female)"]
  J2 = female pin header, 16 pins [form="♀ (female)"]
  IC1 = IC, DIP package, 20 pins [chip_label=IC]

nets:
  N1: J1.pin1, J1.pin2, J1.pin3, J1.pin4, J1.pin16, J2.pin2, J2.pin3, J2.pin4, J2.pin5, J2.pin7, J2.pin8, J2.pin10, J2.pin11, IC1.pin10
  N2: J1.pin5, IC1.pin18
  N3: J1.pin6, IC1.pin17
  N4: J1.pin7, IC1.pin16
  N5: J1.pin8, IC1.pin5
  N6: J1.pin9, IC1.pin4
  N7: J1.pin10, IC1.pin3
  N8: J1.pin11, IC1.pin2
  N9: J1.pin12, IC1.pin1
  N10: J1.pin13, IC1.pin6
  N11: J1.pin14, IC1.pin7
  N12: J1.pin15, IC1.pin8
  N13: J2.pin1, IC1.pin20
  N14: J2.pin6, IC1.pin19
  N15: J2.pin9, IC1.pin15
  N16: J2.pin12, IC1.pin14
  N17: J2.pin13, IC1.pin13
  N18: J2.pin14, IC1.pin12
  N19: J2.pin15, IC1.pin11
  N20: J2.pin16, IC1.pin9

notes:
  M27C4001-35XFI
  to MB7124E
  adapter
